# Fritzing sketch Basic Wiring (saved by Fritzing 0.9.6b)
breadboards: 1

parts:
  DS6 = DS18B20 1-Wire Temperature Sensor [part_number=DS18B20]
  R2 = Resistor [tolerance=±5% resistance=4.7k package="0603 [SMD]"]
  Part2 = BME280 Breakout
  MCU1 = Raspberry Pi Zero
  DS7 = DS18B20 1-Wire Temperature Sensor [part_number=DS18B20]
  DS8 = DS18B20 1-Wire Temperature Sensor [part_number=DS18B20]

nets:
  GND: DS6.GND, Part2.GND, MCU1.pin_9, DS7.GND, DS8.GND
  N1: DS6.DQ, R2.Pin_1, MCU1.pin_7, DS7.DQ, DS8.DQ
  VDD: DS6.VDD, R2.Pin_0, Part2.3.3V, MCU1.pin_1, MCU1.pin_17, DS7.VDD, DS8.VDD
  N2: Part2.SDI/SDA, MCU1.pin_3
  N3: Part2.SCK/SCL, MCU1.pin_5

notes:
  Resistor is 4.7kΩ
  These are the same as the waterproof DS18B20 sensors.
  This is a different looking version of the BME280.
